// Digital circuit Synchronous Sequential Machine.dig as structural Verilog
module Synchronous_Sequential_Machine (
  input  f,
  input  c,
  input  clk,
  input  reset,
  output R,
  output C_2
);

  wire and_1_out, and_2_out, and_3_out, and_4_out, and_5_out, and_6_out, and_7_out, and_8_out, and_9_out,
       and_10_out, and_11_out, and_12_out, cb, fb, or_1_out, or_2_out, or_3_out, q0, q0b, q1, q1b, q2, q2b;

  not not_1 (cb, f);
  not not_2 (fb, c);
  and and_1 (and_1_out, q0, cb);
  and and_2 (and_2_out, q2b, q1b, f, cb);
  and and_3 (and_3_out, q2, q0);
  and and_4 (and_4_out, q1b, f);
  and and_5 (and_5_out, q1b, c);
  and and_6 (and_6_out, q1, fb, cb);
  and and_7 (and_7_out, q2, q1);
  or or_1 (or_1_out, and_1_out, and_2_out, and_3_out);
  or or_2 (or_2_out, and_4_out, and_5_out, and_6_out, and_7_out);
  and and_8 (and_8_out, q2, q0b, c);
  and and_9 (and_9_out, q2, q1);
  and and_10 (and_10_out, q0, f, cb);
  and and_11 (and_11_out, q2, fb, cb);
  and and_12 (and_12_out, q1, q0b, c);
  D_FF_AS d_ff_as_1 (.Set(1'b0), .D(or_3_out), .C(clk), .Clr(reset), .Q(q2), .nQ(q2b));
  D_FF_AS d_ff_as_2 (.Set(1'b0), .D(or_2_out), .C(clk), .Clr(reset), .Q(q1), .nQ(q1b));
  D_FF_AS d_ff_as_3 (.Set(1'b0), .D(or_1_out), .C(clk), .Clr(reset), .Q(q0), .nQ(q0b));
  or or_3 (or_3_out, and_8_out, and_9_out, and_10_out, and_11_out, and_12_out);
  and and_13 (R, q2, q1, q0);
  and and_14 (C_2, q1, q1b, q0b);
endmodule
